# Fritzing sketch picheckvoltage (saved by Fritzing 0.7.12b)
breadboards: 1

parts:
  RaspberryPi1 = Raspberry Pi Model B
  Battery_power_line = female pin header, 2 pins [form="♀ (female)"]
  +5V = female pin header, 2 pins [form="♀ (female)"]
  LOWVOLT = LED - 5mm [color="Yellow (595nm)" package="5 mm [THT]"]
  GOODVOLT = LED - 5mm [color="Green (555nm)" package="5 mm [THT]"]
  R1 = Resistor [tolerance=±5% resistance=330 package=THT]
  R2 = Resistor [tolerance=±5% resistance=330 package=THT]
  C1 = Ceramic Capacitor [capacitance=100nF part_number=100µF voltage=16V package="100 mil [THT, multilayer]"]
  C2 = Ceramic Capacitor [capacitance=10nF voltage=16V part_number=10µF package="100 mil [THT, multilayer]"]
  D1 = Rectifier Diode [part_number=BY299 package="300 mil [THT]"]
  U1 = Voltage Regulator - 5V [part_number=L78S05CV package="TO220 [THT]"]
  IC1 = MCP3008 8-channel 10-bit ADC [part_number=MCP3008]
  R2_2 = Resistor [tolerance=±5% resistance=3.9k package=THT]
  R1_2 = Resistor [tolerance=±5% resistance=10k package=THT]
  R3 = Resistor [tolerance=±5% resistance=330 package=THT]
  Q1 = NPN-Transistor [part_number=BCU81 package="TO92 [THT]"]

nets:
  N1: RaspberryPi1.3V3, IC1.no_name_yet#15, IC1.no_name_yet#16
  N2: RaspberryPi1.GND, Battery_power_line.pin1, +5V.pin1, LOWVOLT.cathode, GOODVOLT.cathode, C1.1, C2.0, IC1.no_name_yet#9, IC1.no_name_yet#14, R2_2.Pin_0, Q1.E
  N3: RaspberryPi1.#17, R2.Pin_1
  N4: RaspberryPi1.#18, R1.Pin_1
  N5: RaspberryPi1.#21, R3.Pin_1
  N6: RaspberryPi1.MOSI, IC1.no_name_yet#11
  N7: RaspberryPi1.MISO, IC1.no_name_yet#12
  N8: RaspberryPi1.SCLK, IC1.no_name_yet#13
  N9: RaspberryPi1.CS0, IC1.no_name_yet#10
  N10: Battery_power_line.pin2, D1.anode, R1_2.Pin_0
  N11: +5V.pin2, C2.1, U1.output_voltage
  N12: LOWVOLT.anode, R2.Pin_0
  N13: GOODVOLT.anode, R1.Pin_0
  N14: C1.0, D1.cathode, U1.input_voltage
  N15: U1.GND, Q1.C
  N16: IC1.no_name_yet#1, R2_2.Pin_1, R1_2.Pin_1
  N17: R3.Pin_0, Q1.B

notes:
  Power line from battery pack
  +5V regulated power line
  Voltage regulator
  Battery voltage measure
  with resistor voltage divider.
  This voltage divider is sized for a battery pack of 8 NiMH batteries (input: 11.2V max; output: about 3.2V max)
  Status LEDs
  “Kill switch“ when battery voltage is really too low

custom parts:
  Raspberry Pi Model B: Raspberry Pi (Model B)
